// Logisim project 20074214_周子渔.circ as structural Verilog: 12 circuits, main circuit main
module main (
  input  in_1
);

  wire AluSrc, clk, J, Memread, MemWrite, MetroReg, nPC_sel, RegDst, RegWrite, zero;
  wire [1:0] Aluctr_1_0, ExtOp_1_0;
  wire [4:0] multiplexer_1_out, rs, rt;
  wire [5:0] opcode;
  wire [15:0] address;
  wire [31:0] ALU_aluout, DM_out, Extender_imm32, gpr_20074214_1_busa, gpr_20074214_1_busb,
       multiplexer_2_out, multiplexer_3_out;

  Clock clock_1 (.out(clk));
  IFU_20074214 ifu_20074214_1 (
    .J(J), .nPC_sel(nPC_sel), .zero(zero), .clk(clk), .reset(in_1), .out({opcode, rs, rt, address}));
  controller_20074214 Controller (
    .funct(address[5:0]), .opcode(opcode), .RegDst(RegDst), .ALUSrc(AluSrc), .Mem2_Reg(MetroReg),
    .Reg_Write(RegWrite), .Memread(Memread), .MemWrite(MemWrite), .nPc_Sel(nPC_sel), .ALU_Op_1_0(Aluctr_1_0),
    .Ext_Op_1_0(ExtOp_1_0), .j(J));
  Multiplexer #(.width(5)) multiplexer_1 (
    .in0(rt), .in1(address[15:11]), .out(multiplexer_1_out), .sel(RegDst));  // open: en
  Multiplexer #(.width(32)) multiplexer_2 (
    .in0(ALU_aluout), .in1(DM_out), .out(multiplexer_2_out), .sel(MetroReg));  // open: en
  GPR_20074214 gpr_20074214_1 (
    .clk(clk), .RegWrite(RegWrite), .\RA读寄存器 (rs), .\RB读寄存器 (rt), .\RW写寄存器 (multiplexer_1_out),
    .WD(multiplexer_2_out), .busA(gpr_20074214_1_busa), .busB(gpr_20074214_1_busb));
  extender_20074214 Extender (.IMM16(address), .ExtOp_1_0(ExtOp_1_0), .IMM32(Extender_imm32));
  Multiplexer #(.width(32)) multiplexer_3 (
    .in0(gpr_20074214_1_busb), .in1(Extender_imm32), .out(multiplexer_3_out), .sel(AluSrc));  // open: en
  _20074214_alu ALU (
    .A(gpr_20074214_1_busa), .B(multiplexer_3_out), .Alu_sel(Aluctr_1_0), .zero(zero), .Aluout(ALU_aluout));
  DM_20074214 DM (
    .data(gpr_20074214_1_busb), .addr(ALU_aluout), .MemWr(MemWrite), .Reset(in_1), .clk(clk), .out(DM_out));

  // Other names for the same wires on the sheet: funct[5:0] = address[5:0]; shamt[4:0] = address[10:6];
  //   rd[4:0] = address[15:11]; reset = in_1

  // Notes on the sheet:
  //   TOP 周子渔 20074214
endmodule

module add4 (
  input  [3:0] A,
  input  [3:0] B,
  input  cin,
  output S0,
  output S1,
  output S2,
  output S3,
  output P_0,
  output G_0
);

  wire and_1_out, and_2_out, and_3_out, and_8_out, and_9_out, and_10_out, and_11_out, C0, C1, C2, C3, G0, G1,
       G2, G3, P0, P1, P2, P3;

  and and_1 (and_1_out, P3, G2);
  and and_2 (and_2_out, P3, P2, G1);
  and and_3 (and_3_out, P3, P2, P1, G0);
  xor xor_1 (P0, A[0], B[0]);
  xor xor_2 (P1, A[1], B[1]);
  xor xor_3 (P2, A[2], B[2]);
  xor xor_4 (P3, A[3], B[3]);
  and and_4 (G0, A[0], B[0]);
  and and_5 (G1, A[1], B[1]);
  and and_6 (G2, A[2], B[2]);
  and and_7 (G3, A[3], B[3]);
  or or_1 (G_0, G3, and_1_out, and_2_out, and_3_out);
  or or_2 (C0, G0, and_8_out);
  and and_8 (and_8_out, cin, P0);
  or or_3 (C1, G1, and_9_out);
  and and_9 (and_9_out, C0, P1);
  or or_4 (C2, G2, and_10_out);
  and and_10 (and_10_out, C1, P2);
  or or_5 (C3, G3, and_11_out);
  and and_11 (and_11_out, C2, P3);
  and and_12 (P_0, P0, P1, P2, P3);
  xor xor_5 (S0, cin, P0);
  xor xor_6 (S1, C0, P1);
  xor xor_7 (S2, C1, P2);
  xor xor_8 (S3, C2, P3);

  // Notes on the sheet:
  //   add4 周子渔20074214
endmodule

module add16 (
  input  [15:0] A,
  input  [15:0] B,
  input  Cin,
  output G_0,
  output P_0,
  output [15:0] S0_S15
);

  wire and_1_out, and_2_out, and_3_out, and_4_out, and_5_out, and_6_out, and_7_out, and_8_out, and_9_out,
       and_10_out, and_11_out, and_12_out, and_13_out, C3, C7, C11, C15, G0, G1, G2, G3, P0, P1, P2, P3;

  add4 add4_1 (
    .A(A[3:0]), .B(B[3:0]), .cin(Cin), .S0(S0_S15[0]), .S1(S0_S15[1]), .S2(S0_S15[2]), .S3(S0_S15[3]),
    .P_0(P0), .G_0(G0));
  add4 add4_2 (
    .A(A[7:4]), .B(B[7:4]), .cin(C3), .S0(S0_S15[4]), .S1(S0_S15[5]), .S2(S0_S15[6]), .S3(S0_S15[7]),
    .P_0(P1), .G_0(G1));
  add4 add4_3 (
    .A(A[11:8]), .B(B[11:8]), .cin(C7), .S0(S0_S15[8]), .S1(S0_S15[9]), .S2(S0_S15[10]), .S3(S0_S15[11]),
    .P_0(P2), .G_0(G2));
  add4 add4_4 (
    .A(A[15:12]), .B(B[15:12]), .cin(C11), .S0(S0_S15[12]), .S1(S0_S15[13]), .S2(S0_S15[14]),
    .S3(S0_S15[15]), .P_0(P3), .G_0(G3));
  and and_1 (and_1_out, Cin, P0);
  and and_2 (and_2_out, P1, G0);
  and and_3 (and_3_out, P1, P0, Cin);
  and and_4 (and_4_out, G1, P2);
  and and_5 (and_5_out, P2, P1, G0);
  and and_6 (and_6_out, P2, P1, P0, Cin);
  and and_7 (and_7_out, G2, P3);
  and and_8 (and_8_out, P2, P1, P3, P0, Cin);
  and and_9 (and_9_out, P2, G1, P3);
  and and_10 (and_10_out, P2, P1, P3, G0);
  or or_1 (C3, G0, and_1_out);
  or or_2 (C7, G1, and_2_out, and_3_out);
  or or_3 (C11, G2, and_4_out, and_5_out, and_6_out);
  or or_4 (C15, G3, and_7_out, and_8_out, and_9_out, and_10_out);
  and and_11 (and_11_out, G2, P3);
  and and_12 (and_12_out, P2, G1, P3);
  and and_13 (and_13_out, P2, P1, P3, G0);
  and and_14 (P_0, P2, P1, P3, P0);
  or or_5 (G_0, G3, and_11_out, and_12_out, and_13_out);

  // Other names for the same wires on the sheet: A0_A3[3:0] = A[3:0]; A4_A7[3:0] = A[7:4]; A8_A11[3:0] = A[11:8];
  //   A12_A15[3:0] = A[15:12]; B0_B3[3:0] = B[3:0]; B4_B7[3:0] = B[7:4]; B8_B11[3:0] = B[11:8];
  //   B12_B15[3:0] = B[15:12]; S0 = S0_S15[0]; S1 = S0_S15[1]; S2 = S0_S15[2]; S3 = S0_S15[3]; S4 = S0_S15[4];
  //   S5 = S0_S15[5]; S6 = S0_S15[6]; S7 = S0_S15[7]; S8 = S0_S15[8]; S9 = S0_S15[9]; S10 = S0_S15[10];
  //   S11 = S0_S15[11]; S12 = S0_S15[12]; S13 = S0_S15[13]; S14 = S0_S15[14]; S15 = S0_S15[15]

  // Notes on the sheet:
  //   add16 周子渔20074214
endmodule

module add32 (
  input  Cin,
  input  [31:0] A,
  input  [31:0] B,
  output [31:0] out_4
);

  wire add16_1_g_0, add16_1_p_0, and_1_out, or_1_out;

  add16 add16_1 (.A(A[15:0]), .B(B[15:0]), .Cin(Cin), .G_0(add16_1_g_0), .P_0(add16_1_p_0), .S0_S15(out_4[15:0]));
  add16 add16_2 (.A(A[31:16]), .B(B[31:16]), .Cin(or_1_out), .S0_S15(out_4[31:16]));  // open: G_0, P_0
  and and_1 (and_1_out, add16_1_p_0, Cin);
  or or_1 (or_1_out, add16_1_g_0, and_1_out);

  // Notes on the sheet:
  //   add32 周子渔20074214
endmodule

module sub32 (
  input  [31:0] A,
  input  [31:0] B,
  output [31:0] S
);

  wire [31:0] add32_1_out_4, not_1_out;

  assign not_1_out = ~B;  // NOT_Gate not_1, 32 bits wide
  add32 add32_1 (.Cin(1'b0), .A(not_1_out), .B(32'h1), .out_4(add32_1_out_4));
  add32 add32_2 (.Cin(1'b0), .A(A), .B(add32_1_out_4), .out_4(S));

  // Notes on the sheet:
  //   sub32 周子渔20074214
endmodule

module or32 (
  input  [31:0] A,
  input  [31:0] B,
  output [31:0] S
);

  assign S = A | B;  // OR_Gate or_1, 32 bits wide

  // Notes on the sheet:
  //   or32 周子渔20074214
endmodule

module _20074214_alu (
  input  [31:0] A,
  input  [31:0] B,
  input  [1:0] Alu_sel,
  output [31:0] Aluout,
  output zero
);

  wire or_1_out;
  wire [31:0] add32_1_out_4, or32_1_s, sub32_1_s;

  add32 add32_1 (.Cin(1'b0), .A(A), .B(B), .out_4(add32_1_out_4));
  sub32 sub32_1 (.A(A), .B(B), .S(sub32_1_s));
  or32 or32_1 (.A(A), .B(B), .S(or32_1_s));
  Multiplexer #(.select(2), .width(32)) multiplexer_1 (
    .in0(add32_1_out_4), .in1(sub32_1_s), .in2(or32_1_s), .out(Aluout), .sel(Alu_sel));  // open: in3, en
  or or_1 (or_1_out, Aluout[31], Aluout[30], Aluout[29], Aluout[28], Aluout[27], Aluout[26], Aluout[25], Aluout[24], Aluout[23], Aluout[22], Aluout[21], Aluout[20], Aluout[19], Aluout[18], Aluout[17], Aluout[16], Aluout[15], Aluout[14], Aluout[13], Aluout[12], Aluout[11], Aluout[10], Aluout[9], Aluout[8], Aluout[7], Aluout[6], Aluout[5], Aluout[4], Aluout[3], Aluout[2], Aluout[1], Aluout[0]);
  not not_1 (zero, or_1_out);

  // Notes on the sheet:
  //   ALU 周子渔20074214
endmodule

// IFU
module IFU_20074214 (
  input  J,
  input  nPC_sel,
  input  zero,
  input  clk,
  input  reset,
  output [31:0] out
);

  wire _26, _27, _28, _29, _30, _31, and_1_out, or_1_out;
  wire [25:0] adder_2_out;
  wire [31:0] adder_1_out, bit_extender_1_out, multiplexer_1_out, multiplexer_2_out, PC_q, shifter_1_out;

  assign bit_extender_1_out = {{16{out[15]}}, out[15:0]};  // Bit_Extender bit_extender_1
  Shifter #(.width(32)) shifter_1 (.in(bit_extender_1_out), .\dist (5'b00010), .out(shifter_1_out));
  and and_1 (and_1_out, nPC_sel, zero);
  Adder #(.width(32)) adder_1 (
    .a({_31, _30, _29, _28, _27, _26, adder_2_out}), .b(shifter_1_out), .out(adder_1_out));  // open: cin, cout
  Adder #(.width(32)) adder_2 (
    .a(PC_q), .b(32'h4), .out({_31, _30, _29, _28, _27, _26, adder_2_out}));  // open: cin, cout
  Multiplexer #(.width(32)) multiplexer_1 (
    .in0(adder_1_out), .in1({_31, _30, _29, _28, out[25:0], 2'b00}), .out(multiplexer_1_out), .sel(J));  // open: en
  or or_1 (or_1_out, J, and_1_out);
  Register #(.width(32)) PC (.D(multiplexer_2_out), .Q(PC_q), .clk(clk), .clr(reset));  // open: en
  Multiplexer #(.width(32)) multiplexer_2 (
    .in0({_31, _30, _29, _28, _27, _26, adder_2_out}), .in1(multiplexer_1_out), .out(multiplexer_2_out),
    .sel(or_1_out));  // open: en
  // Probe on PC_q
  ROM rom_1 (.addr(PC_q[9:2]), .data(out[31:24]));  // open: sel
  ROM rom_2 (.addr(PC_q[9:2]), .data(out[23:16]));  // open: sel
  ROM rom_3 (.addr(PC_q[9:2]), .data(out[15:8]));  // open: sel
  ROM rom_4 (.addr(PC_q[9:2]), .data(out[7:0]));  // open: sel
  // Probe on out

  // Other names for the same wires on the sheet: IMM[15:0] = out[15:0]; JPC[31:2] = {_31, _30, _29, _28, out[25:0]}

  // Notes on the sheet:
  //   IFU 周子渔 20074214
  //   contents of rom_1 (hex, n*v repeats v):
  //   34 34 0 0 1 ac 8c 11 3c 8 34 3c 8
  //   contents of rom_2 (hex, n*v repeats v):
  //   3 6 66 66 2a 9 a 2a b 0 b 9
  //   contents of rom_3 (hex, n*v repeats v):
  //   0 0 40 48 4*0 cd c ef 45 c
  //   contents of rom_4 (hex, n*v repeats v):
  //   93 ae 21 23 21 10 10 2 cd d ef 67 7
endmodule

module extender_20074214 (
  input  [15:0] IMM16,
  input  [1:0] ExtOp_1_0,
  output [31:0] IMM32
);

  wire [31:0] bit_extender_1_out, bit_extender_2_out;

  assign bit_extender_1_out = {{16{1'b0}}, IMM16};  // Bit_Extender bit_extender_1
  assign bit_extender_2_out = {{16{IMM16[15]}}, IMM16};  // Bit_Extender bit_extender_2
  Multiplexer #(.select(2), .width(32)) multiplexer_1 (
    .in0(bit_extender_1_out), .in1(bit_extender_2_out), .in2({IMM16, {16{1'b0}}}), .out(IMM32),
    .sel(ExtOp_1_0));  // open: in3, en

  // Notes on the sheet:
  //   extender 周子渔 20074214
endmodule

module DM_20074214 (
  input  [31:0] data,
  input  [31:0] addr,
  input  MemWr,
  input  Reset,
  input  clk,
  output [31:0] out
);

  RAM #(.bus("separate")) ram_1 (
    .addr(addr[7:0]), .din(data[7:0]), .data(out[7:0]), .str(MemWr), .sel(1'b1), .clk(clk), .clr(Reset));  // open: ld
  RAM #(.bus("separate")) ram_2 (
    .addr(addr[7:0]), .din(data[15:8]), .data(out[15:8]), .str(MemWr), .sel(1'b1), .clk(clk), .clr(Reset));  // open: ld
  RAM #(.bus("separate")) ram_3 (
    .addr(addr[7:0]), .din(data[23:16]), .data(out[23:16]), .str(MemWr), .sel(1'b1), .clk(clk), .clr(Reset));  // open: ld
  RAM #(.bus("separate")) ram_4 (
    .addr(addr[7:0]), .din(data[31:24]), .data(out[31:24]), .str(MemWr), .sel(1'b1), .clk(clk), .clr(Reset));  // open: ld

  // Notes on the sheet:
  //   DM 周子渔 20074214
endmodule

// GPR
module GPR_20074214 (
  input  clk,
  input  RegWrite,
  input  [4:0] \RA读寄存器 ,
  input  [4:0] \RB读寄存器 ,
  input  [4:0] \RW写寄存器 ,
  input  [31:0] WD,
  output [31:0] busA,
  output [31:0] busB
);

  wire demultiplexer_1_out0, demultiplexer_1_out1, demultiplexer_1_out2, demultiplexer_1_out3,
       demultiplexer_1_out4, demultiplexer_1_out5, demultiplexer_1_out6, demultiplexer_1_out7,
       demultiplexer_1_out8, demultiplexer_1_out9, demultiplexer_1_out10, demultiplexer_1_out11,
       demultiplexer_1_out12, demultiplexer_1_out13, demultiplexer_1_out14, demultiplexer_1_out15,
       demultiplexer_1_out16, demultiplexer_1_out17, demultiplexer_1_out18, demultiplexer_1_out19,
       demultiplexer_1_out20, demultiplexer_1_out21, demultiplexer_1_out22, demultiplexer_1_out23,
       demultiplexer_1_out24, demultiplexer_1_out25, demultiplexer_1_out26, demultiplexer_1_out27,
       demultiplexer_1_out28, demultiplexer_1_out29, demultiplexer_1_out30, demultiplexer_1_out31;
  wire [31:0] _1, _2, _3, _4, _5, _6, _7, _8, _9, _10, _11, _12, _13, _14, _15, _16, _17, _18, _19, _20, _21,
       _22, _23, _24, _25, _26, _27, _28, _29, _30, _31;

  Demultiplexer #(.select(5)) demultiplexer_1 (
    .out0(demultiplexer_1_out0), .out1(demultiplexer_1_out1), .out2(demultiplexer_1_out2),
    .out3(demultiplexer_1_out3), .out4(demultiplexer_1_out4), .out5(demultiplexer_1_out5),
    .out6(demultiplexer_1_out6), .out7(demultiplexer_1_out7), .out8(demultiplexer_1_out8),
    .out9(demultiplexer_1_out9), .out10(demultiplexer_1_out10), .out11(demultiplexer_1_out11),
    .out12(demultiplexer_1_out12), .out13(demultiplexer_1_out13), .out14(demultiplexer_1_out14),
    .out15(demultiplexer_1_out15), .out16(demultiplexer_1_out16), .out17(demultiplexer_1_out17),
    .out18(demultiplexer_1_out18), .out19(demultiplexer_1_out19), .out20(demultiplexer_1_out20),
    .out21(demultiplexer_1_out21), .out22(demultiplexer_1_out22), .out23(demultiplexer_1_out23),
    .out24(demultiplexer_1_out24), .out25(demultiplexer_1_out25), .out26(demultiplexer_1_out26),
    .out27(demultiplexer_1_out27), .out28(demultiplexer_1_out28), .out29(demultiplexer_1_out29),
    .out30(demultiplexer_1_out30), .out31(demultiplexer_1_out31), .in(RegWrite), .sel(\RW写寄存器 ));  // open: en
  Register #(.width(32)) register_1 (.D(WD), .en(demultiplexer_1_out0), .clk(clk));  // open: Q, clr
  Register #(.width(32)) register_2 (.D(WD), .en(demultiplexer_1_out1), .Q(_1), .clk(clk));  // open: clr
  Register #(.width(32)) register_3 (.D(WD), .en(demultiplexer_1_out2), .Q(_2), .clk(clk));  // open: clr
  Register #(.width(32)) register_4 (.D(WD), .en(demultiplexer_1_out3), .Q(_3), .clk(clk));  // open: clr
  Register #(.width(32)) register_5 (.D(WD), .en(demultiplexer_1_out4), .Q(_4), .clk(clk));  // open: clr
  Register #(.width(32)) register_6 (.D(WD), .en(demultiplexer_1_out5), .Q(_5), .clk(clk));  // open: clr
  Register #(.width(32)) register_7 (.D(WD), .en(demultiplexer_1_out6), .Q(_6), .clk(clk));  // open: clr
  Register #(.width(32)) register_8 (.D(WD), .en(demultiplexer_1_out7), .Q(_7), .clk(clk));  // open: clr
  Register #(.width(32)) register_9 (.D(WD), .en(demultiplexer_1_out8), .Q(_8), .clk(clk));  // open: clr
  Register #(.width(32)) register_10 (.D(WD), .en(demultiplexer_1_out9), .Q(_9), .clk(clk));  // open: clr
  Register #(.width(32)) register_11 (.D(WD), .en(demultiplexer_1_out10), .Q(_10), .clk(clk));  // open: clr
  Register #(.width(32)) register_12 (.D(WD), .en(demultiplexer_1_out11), .Q(_11), .clk(clk));  // open: clr
  Register #(.width(32)) register_13 (.D(WD), .en(demultiplexer_1_out12), .Q(_12), .clk(clk));  // open: clr
  Register #(.width(32)) register_14 (.D(WD), .en(demultiplexer_1_out13), .Q(_13), .clk(clk));  // open: clr
  Register #(.width(32)) register_15 (.D(WD), .en(demultiplexer_1_out14), .Q(_14), .clk(clk));  // open: clr
  Register #(.width(32)) register_16 (.D(WD), .en(demultiplexer_1_out15), .Q(_15), .clk(clk));  // open: clr
  Register #(.width(32)) register_17 (.D(WD), .en(demultiplexer_1_out16), .Q(_16), .clk(clk));  // open: clr
  Register #(.width(32)) register_18 (.D(WD), .en(demultiplexer_1_out17), .Q(_17), .clk(clk));  // open: clr
  Register #(.width(32)) register_19 (.D(WD), .en(demultiplexer_1_out18), .Q(_18), .clk(clk));  // open: clr
  Register #(.width(32)) register_20 (.D(WD), .en(demultiplexer_1_out19), .Q(_19), .clk(clk));  // open: clr
  Register #(.width(32)) register_21 (.D(WD), .en(demultiplexer_1_out20), .Q(_20), .clk(clk));  // open: clr
  Register #(.width(32)) register_22 (.D(WD), .en(demultiplexer_1_out21), .Q(_21), .clk(clk));  // open: clr
  Register #(.width(32)) register_23 (.D(WD), .en(demultiplexer_1_out22), .Q(_22), .clk(clk));  // open: clr
  Register #(.width(32)) register_24 (.D(WD), .en(demultiplexer_1_out23), .Q(_23), .clk(clk));  // open: clr
  Register #(.width(32)) register_25 (.D(WD), .en(demultiplexer_1_out24), .Q(_24), .clk(clk));  // open: clr
  Register #(.width(32)) register_26 (.D(WD), .en(demultiplexer_1_out25), .Q(_25), .clk(clk));  // open: clr
  Register #(.width(32)) register_27 (.D(WD), .en(demultiplexer_1_out26), .Q(_26), .clk(clk));  // open: clr
  Register #(.width(32)) register_28 (.D(WD), .en(demultiplexer_1_out27), .Q(_27), .clk(clk));  // open: clr
  Register #(.width(32)) register_29 (.D(WD), .en(demultiplexer_1_out28), .Q(_28), .clk(clk));  // open: clr
  Register #(.width(32)) register_30 (.D(WD), .en(demultiplexer_1_out29), .Q(_29), .clk(clk));  // open: clr
  Register #(.width(32)) register_31 (.D(WD), .en(demultiplexer_1_out30), .Q(_30), .clk(clk));  // open: clr
  Register #(.width(32)) register_32 (.D(WD), .en(demultiplexer_1_out31), .Q(_31), .clk(clk));  // open: clr
  Multiplexer #(.select(5), .width(32)) multiplexer_1 (
    .in0({32{1'b0}}), .in1(_1), .in2(_2), .in3(_3), .in4(_4), .in5(_5), .in6(_6), .in7(_7), .in8(_8),
    .in9(_9), .in10(_10), .in11(_11), .in12(_12), .in13(_13), .in14(_14), .in15(_15), .in16(_16), .in17(_17),
    .in18(_18), .in19(_19), .in20(_20), .in21(_21), .in22(_22), .in23(_23), .in24(_24), .in25(_25),
    .in26(_26), .in27(_27), .in28(_28), .in29(_29), .in30(_30), .in31(_31), .out(busA), .sel(\RA读寄存器 ));  // open: en
  Multiplexer #(.select(5), .width(32)) multiplexer_2 (
    .in0({32{1'b0}}), .in1(_1), .in2(_2), .in3(_3), .in4(_4), .in5(_5), .in6(_6), .in7(_7), .in8(_8),
    .in9(_9), .in10(_10), .in11(_11), .in12(_12), .in13(_13), .in14(_14), .in15(_15), .in16(_16), .in17(_17),
    .in18(_18), .in19(_19), .in20(_20), .in21(_21), .in22(_22), .in23(_23), .in24(_24), .in25(_25),
    .in26(_26), .in27(_27), .in28(_28), .in29(_29), .in30(_30), .in31(_31), .out(busB), .sel(\RB读寄存器 ));  // open: en

  // Notes on the sheet:
  //   GPR 周子渔 20074214
endmodule

module controller_20074214 (
  input  [5:0] funct,
  input  [5:0] opcode,
  output j,
  output RegDst,
  output ALUSrc,
  output Mem2_Reg,
  output Reg_Write,
  output Memread,
  output MemWrite,
  output nPc_Sel,
  output [1:0] ALU_Op_1_0,
  output [1:0] Ext_Op_1_0
);

  wire addu_out, beq_out, lw_out, not_2_out, not_3_out, not_4_out, not_5_out, not_7_out, not_8_out,
       not_9_out, not_10_out, not_11_out, not_12_out, ori_out, subu_out, sw_out;

  // NOT_Gate not_1 has open pins: in=funct[5], out=open
  not not_2 (not_2_out, funct[4]);
  not not_3 (not_3_out, funct[2]);
  not not_4 (not_4_out, funct[3]);
  not not_5 (not_5_out, funct[1]);
  // NOT_Gate not_6 has open pins: in=funct[0], out=open
  not not_7 (not_7_out, opcode[5]);
  not not_8 (not_8_out, opcode[4]);
  not not_9 (not_9_out, opcode[2]);
  not not_10 (not_10_out, opcode[3]);
  not not_11 (not_11_out, opcode[1]);
  not not_12 (not_12_out, opcode[0]);
  and addu (addu_out, funct[5], not_2_out, not_4_out, not_3_out, not_5_out, funct[0], not_7_out, not_8_out, not_10_out, not_9_out, not_11_out, not_12_out);
  and subu (subu_out, funct[5], not_2_out, not_4_out, not_3_out, funct[1], funct[0], not_7_out, not_8_out, not_10_out, not_9_out, not_11_out, not_12_out);
  and ori (ori_out, not_7_out, not_8_out, opcode[3], opcode[2], not_11_out, opcode[0]);
  and lw (lw_out, opcode[5], not_8_out, not_10_out, not_9_out, opcode[1], opcode[0]);
  and sw (sw_out, opcode[5], not_8_out, opcode[3], not_9_out, opcode[1], opcode[0]);
  and beq (beq_out, not_7_out, not_8_out, not_10_out, opcode[2], not_11_out, not_12_out);
  and lui (Ext_Op_1_0[1], not_7_out, not_8_out, opcode[3], opcode[2], opcode[1], opcode[0]);
  and u_j (lw_out, not_7_out, not_8_out, not_10_out, not_9_out, opcode[1], not_12_out);
  or u_RegDst (RegDst, addu_out, subu_out);
  or u_ALUSrc (ALUSrc, ori_out, lw_out, sw_out, Ext_Op_1_0[1]);
  buf u_Mem2_Reg (Mem2_Reg, lw_out);  // OR_Gate
  or u_Reg_Write (Reg_Write, addu_out, subu_out, Ext_Op_1_0[1], ori_out, lw_out);
  buf u_Memread (Memread, lw_out);  // OR_Gate
  buf u_MemWrite (MemWrite, sw_out);  // OR_Gate
  buf u_nPc_Sel (nPc_Sel, beq_out);  // OR_Gate
  buf ALU_Op1 (ALU_Op_1_0[1], ori_out);  // OR_Gate
  or ALU_Op2 (ALU_Op_1_0[0], subu_out, beq_out);
  or Ext_Op_2 (Ext_Op_1_0[0], lw_out, sw_out);
  buf j_2 (j, lw_out);  // OR_Gate

  // Notes on the sheet:
  //   000000 addu
  //   000000 subu
  //   001101 ori
  //   100011 lw
  //   101011 sw
  //   000100 beq
  //   001111 lui
  //   000010 j
  //   controller 周子渔 20074214
endmodule
